# Fritzing sketch LightLogger (saved by Fritzing 0.9.10b)
breadboards: 1

parts:
  Part3 = Arduino Nano 33 IoT
  Part4 = Adafruit TCS34725 RGB Color Sensor [part_number="Adafruit #1334"]

nets:
  GND: Part3.GND, Part4.GND, Part4.LED_EN
  N1: Part3.A5/SCL, Part4.SCL
  N2: Part3.A4/SDA, Part4.SDA
  3V3: Part3.3V3, Part4.VIN

custom parts:
  Arduino Nano 33 IoT: The Arduino Nano 33 IoT is a small, complete, and breadboard-friendly board based on the Arm® Cortex®-M0 32-bit SAMD21. It has onboard WiFi and Bluetooth® connectivity through a u-blox NINA-W10 chipset. Secure communication is ensured through the Microchip® ECC608 crypto chip. It also has 6-axis LSM6DS3 IMU.
  Adafruit TCS34725 RGB Color Sensor: Your electronics can now see in dazzling color with this lovely color light sensor. We found the best color sensor on the market, the TCS34725, which has RGB and Clear light sensing elements. An IR blocking filter, integrated on-chip and localized to the color sensing photodiodes, minimizes the IR spectral component of the incoming light and allows color measurements to be made accurately. The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
